# Fritzing sketch arduino (saved by Fritzing 0.9.6b)
breadboards: 1

parts:
  Composant1 = Arduino Nano (Rev3.0)
  ZS-042_RTC1 = ZS-042 RTC Module
  U1 = BUTTON-CONDUCTIVE [package=button-conductive]
  M1 = Stepper Motor - Bipolar

nets:
  N1: Composant1.D4, U1.2
  N2: Composant1.D8, M1.D
  N3: Composant1.D9, M1.B
  N4: Composant1.D10, M1.C
  N5: Composant1.D11/MOSI, M1.A
  GND: Composant1.GND, ZS-042_RTC1.GND, U1.1
  5V: Composant1.5V, ZS-042_RTC1.VCC
  N6: Composant1.A5, ZS-042_RTC1.SCL
  N7: Composant1.A4, ZS-042_RTC1.SDA
